// Logisim project vending_machine.circ as structural Verilog: 12 circuits, main circuit main
module main (
  input  in_1,
  input  [15:0] in_2,
  input  [15:0] in_3,
  output [15:0] out_4
);

  wire button_1_out, button_2_out, clock_1_out;
  wire [15:0] undriven;
  wire [31:0] display_module_1_out_7, display_module_1_out_8, display_module_1_out_11,
       display_module_1_out_12, display_module_1_out_13, display_module_1_out_14, display_module_1_out_15,
       display_module_1_out_16, display_module_1_out_17, display_module_1_out_18, display_module_1_out_19,
       display_module_1_out_20, display_module_1_out_21, display_module_1_out_22, display_module_1_out_23,
       display_module_1_out_24, display_module_1_out_25, display_module_1_out_26, display_module_1_out_27,
       display_module_1_out_28, display_module_1_out_29, display_module_1_out_30, display_module_1_out_31,
       display_module_1_out_32, display_module_1_out_33, display_module_1_out_34, display_module_1_out_35,
       display_module_1_out_36, display_module_1_out_37, display_module_1_out_38, display_module_1_out_39,
       rom_1_data;

  Clock #(.highDuration(1), .lowDuration(1)) clock_1 (.out(clock_1_out));
  ROM #(.addrWidth(16), .dataWidth(32), .Select("low")) rom_1 (.addr(undriven), .data(rom_1_data));
  DotMatrix #(.inputtype("column"), .matrixcols(32), .matrixrows(32), .persist(0), .dotshape("square")) dotmatrix_1 (
    .col0(display_module_1_out_7), .col1(display_module_1_out_7), .col2(display_module_1_out_12),
    .col3(display_module_1_out_14), .col4(display_module_1_out_16), .col5(display_module_1_out_18),
    .col6(display_module_1_out_20), .col7(display_module_1_out_22), .col8(display_module_1_out_24),
    .col9(display_module_1_out_26), .col10(display_module_1_out_28), .col11(display_module_1_out_30),
    .col12(display_module_1_out_32), .col13(display_module_1_out_34), .col14(display_module_1_out_36),
    .col15(display_module_1_out_38), .col16(display_module_1_out_8), .col17(display_module_1_out_11),
    .col18(display_module_1_out_13), .col19(display_module_1_out_15), .col20(display_module_1_out_17),
    .col21(display_module_1_out_19), .col22(display_module_1_out_21), .col23(display_module_1_out_23),
    .col24(display_module_1_out_25), .col25(display_module_1_out_27), .col26(display_module_1_out_29),
    .col27(display_module_1_out_31), .col28(display_module_1_out_33), .col29(display_module_1_out_35),
    .col30(display_module_1_out_37), .col31(display_module_1_out_39));
  display_module display_module_1 (
    .Add_Signal(button_1_out), .Sub_Signal(button_2_out), .WE(in_1), .WE_Num(in_2), .Max_Num(in_3),
    .Clk(clock_1_out), .out_7(display_module_1_out_7), .out_8(display_module_1_out_8),
    .out_10(display_module_1_out_7), .out_11(display_module_1_out_11), .out_12(display_module_1_out_12),
    .out_13(display_module_1_out_13), .out_14(display_module_1_out_14), .out_15(display_module_1_out_15),
    .out_16(display_module_1_out_16), .out_17(display_module_1_out_17), .out_18(display_module_1_out_18),
    .out_19(display_module_1_out_19), .out_20(display_module_1_out_20), .out_21(display_module_1_out_21),
    .out_22(display_module_1_out_22), .out_23(display_module_1_out_23), .out_24(display_module_1_out_24),
    .out_25(display_module_1_out_25), .out_26(display_module_1_out_26), .out_27(display_module_1_out_27),
    .out_28(display_module_1_out_28), .out_29(display_module_1_out_29), .out_30(display_module_1_out_30),
    .out_31(display_module_1_out_31), .out_32(display_module_1_out_32), .out_33(display_module_1_out_33),
    .out_34(display_module_1_out_34), .out_35(display_module_1_out_35), .out_36(display_module_1_out_36),
    .out_37(display_module_1_out_37), .out_38(display_module_1_out_38), .out_39(display_module_1_out_39),
    .Num(out_4));
  Button button_1 (.out(button_1_out));
  Button button_2 (.out(button_2_out));

  // Notes on the sheet:
  //   contents of rom_1 (hex, n*v repeats v):
  //   37*0 7fffff0 3c000010 3400001c 2400001e 2407801a 240cb01a 2410b81a 24312c1a 2421641a 2421441a
  //   2423441a 2422c41a 24228c1a 2412881a 240ab01a 2406e01a 2400001e 3400001e 3ffffffc 2ffffff0 9*0 e000
  //   1b800 1e0cc0 720c60 c20c20 1820c00 1220c00 3220c00 2020c00 6820c00 6920c00 41a0c00 4120c00 5820c00
  //   4020c00 4020c00 5920c00 79a0c00 2120c00 2220c00 3720c00 1020c00 1820c00 c20c20 720c60 1e0cc0 1b800
  //   1f000 13*0 1ffffe 3e827e3 7f882003 90082003 80082003 80002003 98002003 ff882003 3f87fe3 3ffffe 3800c
  //   19*0 3ffffc0 3ffffe0 6c001f0 6c001f0 5*6c001b0 6c101b0 6cf01b0 6c001f0 6c003e0 3ffffe0 3ffffc0 10*0
  //   26000000 2a000000 2a000000 3a000000 3a060000 1a0ffe00 1a080ffc a08000e a08ffe2 5*2a080002 6af80002
  //   ebd80002 2b080002 6cf80002 edf80002 ef880002 2ef80006 eff80006 ef880006 280c03fc 320ffff0 ff000 6*0
  //   700 3e0 f80 10c0 21c0 27e0 47e0 4fe0 4fe0 8fc0 9fc0 9fc0 3fc0 13f80 1ff80 3ff00 7ff00 ffe00 3ffe00
  //   7ffc00 fffc00 fff800 1fff000 5ffe000 3ffc000 3ff8000 37e0000 3000000 1000000 11*0 ffffc f90406
  //   7810403 fc010403 90010403 f0010401 90010401 9c010403 77c10403 1fbfc07 1ffffe 13*0 1f80 fff0 3b038
  //   e5808 18340c 301a04 600e0c d0000c 16c0008 3360018 61a0010 40e0030 c000060 8000040 1c0000c0 1b000180
  //   1d800300 26c00600 33000c00 30c01800 30003000 30006000 3000c000 10038000 10060000 181c0000 df00000
  //   3c00000 5*0 ff000 3ffc00 f00f00 1c00380 38101c0 70380e0 6010060 c000030 c000030 18800318 19c00318
  //   18800018 18000018 18018018 18018018 18000018 18000018 c600030 c600630 6000660 70004e0 38301c0
  //   1c30380 f00f00 3ffc00 ff000 5*0 1ff800 600600 1800180 30000c0 6000060 c000030 8000010 1000c008
  //   1000e008 20007004 20003804 20001c04 20003804 20007004 2000e004 2001c004 20038004 20070004 200e0004
  //   101c0008 10180008 8000010 c000030 6000060 30000c0 1800180 600600 1ff800 4*0 1ff800 600600 1800180
  //   30000c0 6000060 c000030 8000010 10000008 10300c08 20381c04 201c3804 200e7004 2007e004 2003c004
  //   2003c004 2007e004 200e7004 201c3804 20381c04 10300c08 10000008 8000010 c000030 6000060 30000c0
  //   1800180 600600 1ff800 6*0 70 f8 1fc 1fc 3fc f803fc 7fe03fc 1fff07fc 1ffffffc 3ffffffc 3ffffcc4
  //   3ffffc00 3ffffc00 3ffffcf4 1ffffffc 1fff8ffc fff07fc 3fc03fc 1003fc 3fc 1fc 1f8 f8
endmodule

module Goods_selection (
  input  [15:0] ProductNumber,
  input  CLK,
  output [15:0] Addr,
  output [4:0] \sequence 
);

  wire comparator_1_eq, comparator_1_gt, comparator_2_gt, comparator_3_eq, not_1_out, not_2_out, or_1_out,
       or_2_out;
  wire [15:0] adder_1_out, multiplier_1_out;

  Multiplier #(.width(16)) multiplier_1 (.a(ProductNumber), .b(16'h20), .out(multiplier_1_out));  // open: cin, cout
  Adder #(.width(16)) adder_1 (.a(multiplier_1_out), .b(16'h20), .out(adder_1_out), .cin(1'b0));  // open: cout
  not not_1 (not_1_out, 1'b0);
  not not_2 (not_2_out, 1'b0);
  Counter #(.width(16), .max('hffff), .ongoal("wrap"), .trigger("rising"), .behavior("new")) counter_1 (
    .load(or_2_out), .D(multiplier_1_out), .count(not_1_out), .Q(Addr), .clk(CLK), .clr(1'b0), .preset(1'b0),
    .down(1'b0));  // open: carry
  Comparator #(.width(16), .mode("twosComplement")) comparator_1 (
    .a(Addr), .b(adder_1_out), .gt(comparator_1_gt), .eq(comparator_1_eq));  // open: lt
  Comparator #(.width(16), .mode("twosComplement")) comparator_2 (
    .a(multiplier_1_out), .b(Addr), .gt(comparator_2_gt));  // open: eq, lt
  Comparator #(.width(16), .mode("twosComplement")) comparator_3 (
    .a({16{1'b0}}), .b(Addr), .eq(comparator_3_eq));  // open: gt, lt
  Counter #(.width(5), .max('h1f), .ongoal("wrap"), .trigger("rising"), .behavior("new")) counter_2 (
    .load(1'b0), .count(not_2_out), .Q(\sequence ), .clk(CLK), .clr(or_2_out), .preset(1'b0), .down(1'b0));  // open: D, carry
  or or_1 (or_1_out, comparator_1_gt, comparator_1_eq);
  or or_2 (or_2_out, or_1_out, comparator_2_gt, comparator_3_eq);

  // Notes on the sheet:
  //   结束地址
  //   地址寄存器
  //   点阵位置寄存器
  //   大于等于结束地址
  //   小于开始地址
  //   等于0地址
endmodule

module Goods_selection_add_sub (
  input  [15:0] W_Num,
  input  WE,
  input  [15:0] Max_Nun,
  input  Add_Signal,
  input  Sub_Signal,
  input  CLK,
  output [15:0] Output_Num
);

  wire and_1_out, comparator_1_gt, comparator_2_lt, multiplexer_3_out, nor_1_out, not_1_out, not_2_out,
       or_1_out;
  wire [15:0] adder_1_out, adder_2_out, bit_extender_1_out, bit_extender_2_out, multiplexer_1_out,
       multiplexer_2_out, subtractor_1_out;

  Adder #(.width(16)) adder_1 (.a(Max_Nun), .b(16'h1), .out(adder_1_out));  // open: cin, cout
  assign bit_extender_1_out = {{15{1'b0}}, Add_Signal};  // Bit_Extender bit_extender_1
  assign bit_extender_2_out = {{15{1'b0}}, Sub_Signal};  // Bit_Extender bit_extender_2
  Comparator #(.width(16), .mode("twosComplement")) comparator_1 (
    .a(adder_1_out), .b(Output_Num), .gt(comparator_1_gt));  // open: eq, lt
  Adder #(.width(16)) adder_2 (.a(bit_extender_1_out), .b(Output_Num), .out(adder_2_out));  // open: cin, cout
  not not_1 (not_1_out, comparator_1_gt);
  Comparator #(.width(16), .mode("twosComplement")) comparator_2 (
    .a(Output_Num), .b({16{1'b0}}), .lt(comparator_2_lt));  // open: gt, eq
  Multiplexer #(.select(1), .width(16), .disabled("Z"), .enable("false")) multiplexer_1 (
    .in0(adder_2_out), .in1(subtractor_1_out), .out(multiplexer_1_out), .sel(Sub_Signal));
  Subtractor #(.width(16)) subtractor_1 (
    .a(Output_Num), .b(bit_extender_2_out), .out(subtractor_1_out));  // open: bin, bout
  not not_2 (not_2_out, WE);
  or or_1 (or_1_out, not_1_out, comparator_2_lt);
  Multiplexer #(.select(1), .width(16), .disabled("Z"), .enable("false")) multiplexer_2 (
    .in0(W_Num), .in1(multiplexer_1_out), .out(multiplexer_2_out), .sel(not_2_out));
  nor nor_1 (nor_1_out, Sub_Signal, Add_Signal);
  and and_1 (and_1_out, not_2_out, or_1_out);
  Multiplexer #(.select(1), .width(1), .disabled("Z"), .enable("false")) multiplexer_3 (
    .in0(CLK), .in1(nor_1_out), .out(multiplexer_3_out), .sel(not_2_out));
  Register #(.width(16), .trigger("rising"), .Select("low")) register_1 (
    .D(multiplexer_2_out), .Q(Output_Num), .clk(multiplexer_3_out), .clr(and_1_out));  // open: en
endmodule

module display_module (
  input  Add_Signal,
  input  Sub_Signal,
  input  WE,
  input  [15:0] WE_Num,
  input  [15:0] Max_Num,
  input  Clk,
  output [31:0] out_7,
  output [31:0] out_8,
  output [15:0] Num,
  output [31:0] out_10,
  output [31:0] out_11,
  output [31:0] out_12,
  output [31:0] out_13,
  output [31:0] out_14,
  output [31:0] out_15,
  output [31:0] out_16,
  output [31:0] out_17,
  output [31:0] out_18,
  output [31:0] out_19,
  output [31:0] out_20,
  output [31:0] out_21,
  output [31:0] out_22,
  output [31:0] out_23,
  output [31:0] out_24,
  output [31:0] out_25,
  output [31:0] out_26,
  output [31:0] out_27,
  output [31:0] out_28,
  output [31:0] out_29,
  output [31:0] out_30,
  output [31:0] out_31,
  output [31:0] out_32,
  output [31:0] out_33,
  output [31:0] out_34,
  output [31:0] out_35,
  output [31:0] out_36,
  output [31:0] out_37,
  output [31:0] out_38,
  output [31:0] out_39
);

  wire decoder_1_out0, decoder_1_out1, decoder_1_out2, decoder_1_out3, decoder_1_out4, decoder_1_out5,
       decoder_1_out6, decoder_1_out7, decoder_1_out8, decoder_1_out9, decoder_1_out10, decoder_1_out11,
       decoder_1_out12, decoder_1_out13, decoder_1_out14, decoder_1_out15, decoder_1_out16, decoder_1_out17,
       decoder_1_out18, decoder_1_out19, decoder_1_out20, decoder_1_out21, decoder_1_out22, decoder_1_out23,
       decoder_1_out24, decoder_1_out25, decoder_1_out26, decoder_1_out27, decoder_1_out28, decoder_1_out29,
       decoder_1_out30, decoder_1_out31;
  wire [4:0] goods_selection_1_sequence;
  wire [15:0] goods_selection_1_addr;
  wire [31:0] rom_1_data;

  Goods_selection_add_sub goods_selection_add_sub_1 (
    .W_Num(WE_Num), .WE(WE), .Max_Nun(Max_Num), .Add_Signal(Add_Signal), .Sub_Signal(Sub_Signal), .CLK(Clk),
    .Output_Num(Num));
  Goods_selection goods_selection_1 (
    .ProductNumber(Num), .CLK(Clk), .Addr(goods_selection_1_addr), .\sequence (goods_selection_1_sequence));
  ROM #(.addrWidth(16), .dataWidth(32), .Select("low")) rom_1 (.addr(goods_selection_1_addr), .data(rom_1_data));
  Decoder #(.select(5), .tristate("false"), .disabled(0), .enable("false")) decoder_1 (
    .out0(decoder_1_out0), .out1(decoder_1_out1), .out2(decoder_1_out2), .out3(decoder_1_out3),
    .out4(decoder_1_out4), .out5(decoder_1_out5), .out6(decoder_1_out6), .out7(decoder_1_out7),
    .out8(decoder_1_out8), .out9(decoder_1_out9), .out10(decoder_1_out10), .out11(decoder_1_out11),
    .out12(decoder_1_out12), .out13(decoder_1_out13), .out14(decoder_1_out14), .out15(decoder_1_out15),
    .out16(decoder_1_out16), .out17(decoder_1_out17), .out18(decoder_1_out18), .out19(decoder_1_out19),
    .out20(decoder_1_out20), .out21(decoder_1_out21), .out22(decoder_1_out22), .out23(decoder_1_out23),
    .out24(decoder_1_out24), .out25(decoder_1_out25), .out26(decoder_1_out26), .out27(decoder_1_out27),
    .out28(decoder_1_out28), .out29(decoder_1_out29), .out30(decoder_1_out30), .out31(decoder_1_out31),
    .sel(goods_selection_1_sequence));
  Register #(.width(32), .trigger("rising"), .Select("low")) register_1 (
    .D(rom_1_data), .en(decoder_1_out0), .Q(out_7), .clk(Clk), .cs(1'b0));  // open: clr, preset
  Register #(.width(32), .trigger("rising"), .Select("low")) register_2 (
    .D(rom_1_data), .en(decoder_1_out2), .Q(out_12), .clk(Clk), .cs(1'b0));  // open: clr, preset
  Register #(.width(32), .trigger("rising"), .Select("low")) register_3 (
    .D(rom_1_data), .en(decoder_1_out4), .Q(out_16), .clk(Clk), .cs(1'b0));  // open: clr, preset
  Register #(.width(32), .trigger("rising"), .Select("low")) register_4 (
    .D(rom_1_data), .en(decoder_1_out6), .Q(out_20), .clk(Clk), .cs(1'b0));  // open: clr, preset
  Register #(.width(32), .trigger("rising"), .Select("low")) register_5 (
    .D(rom_1_data), .en(decoder_1_out8), .Q(out_24), .clk(Clk), .cs(1'b0));  // open: clr, preset
  Register #(.width(32), .trigger("rising"), .Select("low")) register_6 (
    .D(rom_1_data), .en(decoder_1_out10), .Q(out_28), .clk(Clk), .cs(1'b0));  // open: clr, preset
  Register #(.width(32), .trigger("rising"), .Select("low")) register_7 (
    .D(rom_1_data), .en(decoder_1_out12), .Q(out_32), .clk(Clk), .cs(1'b0));  // open: clr, preset
  Register #(.width(32), .trigger("rising"), .Select("low")) register_8 (
    .D(rom_1_data), .en(decoder_1_out14), .Q(out_36), .clk(Clk), .cs(1'b0));  // open: clr, preset
  Register #(.width(32), .trigger("rising"), .Select("low")) register_9 (
    .D(rom_1_data), .en(decoder_1_out16), .Q(out_8), .clk(Clk), .cs(1'b0));  // open: clr, preset
  Register #(.width(32), .trigger("rising"), .Select("low")) register_10 (
    .D(rom_1_data), .en(decoder_1_out18), .Q(out_13), .clk(Clk), .cs(1'b0));  // open: clr, preset
  Register #(.width(32), .trigger("rising"), .Select("low")) register_11 (
    .D(rom_1_data), .en(decoder_1_out20), .Q(out_17), .clk(Clk), .cs(1'b0));  // open: clr, preset
  Register #(.width(32), .trigger("rising"), .Select("low")) register_12 (
    .D(rom_1_data), .en(decoder_1_out22), .Q(out_21), .clk(Clk), .cs(1'b0));  // open: clr, preset
  Register #(.width(32), .trigger("rising"), .Select("low")) register_13 (
    .D(rom_1_data), .en(decoder_1_out24), .Q(out_25), .clk(Clk), .cs(1'b0));  // open: clr, preset
  Register #(.width(32), .trigger("rising"), .Select("low")) register_14 (
    .D(rom_1_data), .en(decoder_1_out26), .Q(out_29), .clk(Clk), .cs(1'b0));  // open: clr, preset
  Register #(.width(32), .trigger("rising"), .Select("low")) register_15 (
    .D(rom_1_data), .en(decoder_1_out28), .Q(out_33), .clk(Clk), .cs(1'b0));  // open: clr, preset
  Register #(.width(32), .trigger("rising"), .Select("low")) register_16 (
    .D(rom_1_data), .en(decoder_1_out30), .Q(out_37), .clk(Clk), .cs(1'b0));  // open: clr, preset
  Register #(.width(32), .trigger("rising"), .Select("low")) register_17 (
    .D(rom_1_data), .en(decoder_1_out1), .Q(out_10), .clk(Clk), .cs(1'b0));  // open: clr, preset
  Register #(.width(32), .trigger("rising"), .Select("low")) register_18 (
    .D(rom_1_data), .en(decoder_1_out3), .Q(out_14), .clk(Clk), .cs(1'b0));  // open: clr, preset
  Register #(.width(32), .trigger("rising"), .Select("low")) register_19 (
    .D(rom_1_data), .en(decoder_1_out5), .Q(out_18), .clk(Clk), .cs(1'b0));  // open: clr, preset
  Register #(.width(32), .trigger("rising"), .Select("low")) register_20 (
    .D(rom_1_data), .en(decoder_1_out7), .Q(out_22), .clk(Clk), .cs(1'b0));  // open: clr, preset
  Register #(.width(32), .trigger("rising"), .Select("low")) register_21 (
    .D(rom_1_data), .en(decoder_1_out9), .Q(out_26), .clk(Clk), .cs(1'b0));  // open: clr, preset
  Register #(.width(32), .trigger("rising"), .Select("low")) register_22 (
    .D(rom_1_data), .en(decoder_1_out11), .Q(out_30), .clk(Clk), .cs(1'b0));  // open: clr, preset
  Register #(.width(32), .trigger("rising"), .Select("low")) register_23 (
    .D(rom_1_data), .en(decoder_1_out13), .Q(out_34), .clk(Clk), .cs(1'b0));  // open: clr, preset
  Register #(.width(32), .trigger("rising"), .Select("low")) register_24 (
    .D(rom_1_data), .en(decoder_1_out15), .Q(out_38), .clk(Clk), .cs(1'b0));  // open: clr, preset
  Register #(.width(32), .trigger("rising"), .Select("low")) register_25 (
    .D(rom_1_data), .en(decoder_1_out17), .Q(out_11), .clk(Clk), .cs(1'b0));  // open: clr, preset
  Register #(.width(32), .trigger("rising"), .Select("low")) register_26 (
    .D(rom_1_data), .en(decoder_1_out19), .Q(out_15), .clk(Clk), .cs(1'b0));  // open: clr, preset
  Register #(.width(32), .trigger("rising"), .Select("low")) register_27 (
    .D(rom_1_data), .en(decoder_1_out21), .Q(out_19), .clk(Clk), .cs(1'b0));  // open: clr, preset
  Register #(.width(32), .trigger("rising"), .Select("low")) register_28 (
    .D(rom_1_data), .en(decoder_1_out23), .Q(out_23), .clk(Clk), .cs(1'b0));  // open: clr, preset
  Register #(.width(32), .trigger("rising"), .Select("low")) register_29 (
    .D(rom_1_data), .en(decoder_1_out25), .Q(out_27), .clk(Clk), .cs(1'b0));  // open: clr, preset
  Register #(.width(32), .trigger("rising"), .Select("low")) register_30 (
    .D(rom_1_data), .en(decoder_1_out27), .Q(out_31), .clk(Clk), .cs(1'b0));  // open: clr, preset
  Register #(.width(32), .trigger("rising"), .Select("low")) register_31 (
    .D(rom_1_data), .en(decoder_1_out29), .Q(out_35), .clk(Clk), .cs(1'b0));  // open: clr, preset
  Register #(.width(32), .trigger("rising"), .Select("low")) register_32 (
    .D(rom_1_data), .en(decoder_1_out31), .Q(out_39), .clk(Clk), .cs(1'b0));  // open: clr, preset
endmodule

module coin_action (
  input  Un_money,
  input  _5Y_signal,
  input  _1Y_signal,
  input  _0_5Y_signal,
  input  Clr,
  input  _5Y_W,
  input  [15:0] _5Y_Wn,
  input  _1Y_W,
  input  [15:0] _1Y_Wn,
  input  _0_5Y_W,
  input  [15:0] _0_5Y_Wn,
  output Mistake,
  output [15:0] Money_2,
  output [15:0] _5Y,
  output [15:0] _1Y,
  output [15:0] _0_5
);

  wire CLK, comparator_1_lt;
  wire [15:0] adder_1_out, coin_action_add_module_1_output_num, multiplier_1_out, multiplier_2_out;

  Clock #(.highDuration(1), .lowDuration(1)) u_CLK (.out(CLK));
  coin_action_add_module coin_action_add_module_1 (
    .WE_Num({16{1'b0}}), .WE(1'b0), .Clr(Clr), .Add_Signal(Un_money), .Clk(CLK),
    .Output_Num(coin_action_add_module_1_output_num));
  coin_action_add_module coin_action_add_module_2 (
    .WE_Num(_5Y_Wn), .WE(_5Y_W), .Clr(Clr), .Add_Signal(_5Y_signal), .Clk(CLK), .Output_Num(_5Y));
  coin_action_add_module coin_action_add_module_3 (
    .WE_Num(_1Y_Wn), .WE(_1Y_W), .Clr(Clr), .Add_Signal(_1Y_signal), .Clk(CLK), .Output_Num(_1Y));
  coin_action_add_module coin_action_add_module_4 (
    .WE_Num(_0_5Y_Wn), .WE(_0_5Y_W), .Clr(Clr), .Add_Signal(_0_5Y_signal), .Clk(CLK), .Output_Num(_0_5));
  Comparator #(.width(16), .mode("twosComplement")) comparator_1 (
    .a(coin_action_add_module_1_output_num), .b(16'h1), .lt(comparator_1_lt));  // open: gt, eq
  not not_1 (Mistake, comparator_1_lt);
  Multiplier #(.width(16)) multiplier_1 (.a(_5Y), .b(16'ha), .out(multiplier_1_out));  // open: cin, cout
  Multiplier #(.width(16)) multiplier_2 (.a(_1Y), .b(16'h2), .out(multiplier_2_out));  // open: cin, cout
  Adder #(.width(16)) adder_1 (.a(multiplier_2_out), .b(_0_5), .out(adder_1_out));  // open: cin, cout
  Adder #(.width(16)) adder_2 (.a(multiplier_1_out), .b(adder_1_out), .out(Money_2));  // open: cin, cout

  // Other names for the same wires on the sheet: _0_5_yuan = _0_5Y_signal; _1_yuan = _1Y_signal; _5_yuan = _5Y_signal;
  //   W2 = _5Y_W; W3 = _1Y_W; W4 = _0_5Y_W; Wn2[15:0] = _5Y_Wn; Wn3[15:0] = _1Y_Wn; Wn4[15:0] = _0_5Y_Wn
endmodule

module coin_action_add_module (
  input  [15:0] WE_Num,
  input  WE,
  input  Clr,
  input  Add_Signal,
  input  Clk,
  output [15:0] Output_Num
);

  wire and_1_out, comparator_1_gt, comparator_2_lt, multiplexer_2_out, not_1_out, not_2_out, not_3_out,
       or_1_out, or_2_out;
  wire [15:0] adder_1_out, bit_extender_1_out, multiplexer_1_out;

  assign bit_extender_1_out = {{15{1'b0}}, Add_Signal};  // Bit_Extender bit_extender_1
  Comparator #(.width(16), .mode("twosComplement")) comparator_1 (
    .a(16'hfff), .b(Output_Num), .gt(comparator_1_gt));  // open: eq, lt
  not not_1 (not_1_out, comparator_1_gt);
  Comparator #(.width(16), .mode("twosComplement")) comparator_2 (
    .a(Output_Num), .b({16{1'b0}}), .lt(comparator_2_lt));  // open: gt, eq
  Adder #(.width(16)) adder_1 (.a(bit_extender_1_out), .b(Output_Num), .out(adder_1_out));  // open: cin, cout
  not not_2 (not_2_out, Add_Signal);
  not not_3 (not_3_out, WE);
  or or_1 (or_1_out, not_1_out, comparator_2_lt);
  Multiplexer #(.select(1), .width(16), .disabled("Z"), .enable("false")) multiplexer_1 (
    .in0(WE_Num), .in1(adder_1_out), .out(multiplexer_1_out), .sel(not_3_out));
  and and_1 (and_1_out, not_3_out, or_1_out);
  Multiplexer #(.select(1), .width(1), .disabled("Z"), .enable("false")) multiplexer_2 (
    .in0(Clk), .in1(not_2_out), .out(multiplexer_2_out), .sel(not_3_out));
  or or_2 (or_2_out, Clr, and_1_out);
  Register #(.width(16), .trigger("rising"), .Select("low")) register_1 (
    .D(multiplexer_1_out), .Q(Output_Num), .clk(multiplexer_2_out), .clr(or_2_out));  // open: en
endmodule

module Coin_control_module (
  input  \确认 ,
  input  Clk,
  input  [15:0] Num,
  input  in_4,
  input  in_5,
  input  in_6,
  input  in_7,
  output [15:0] out_8
);

  wire and_1_out, button_1_out, button_2_out, button_3_out, button_4_out, comparator_1_gt, comparator_2_gt,
       not_1_out, undriven;
  wire [15:0] coin_action_1__0_5, coin_action_1__1y, coin_action_1__5y;
  wire [31:0] adder_1_out, adder_2_out, adder_3_out, bit_extender_1_out, bit_extender_2_out,
       bit_extender_3_out, bit_extender_4_out, money_memory_1__0_5y, money_memory_1__1y, money_memory_1__5y,
       storehouse_module_1_commodity_num, storehouse_module_1_commodity_price;

  Button button_1 (.out(button_1_out));
  Button button_2 (.out(button_2_out));
  Button button_3 (.out(button_3_out));
  Button button_4 (.out(button_4_out));
  storehouse_module storehouse_module_1 (
    .Num(Num), .Clk(Clk), .Commodity_num(storehouse_module_1_commodity_num),
    .Commodity_price(storehouse_module_1_commodity_price));  // open: Wn_signal, Wn_data, Wp_signal, Wn_data_2
  coin_action coin_action_1 (
    .Clr(in_4), ._5Y_W(in_5), ._1Y_W(in_6), ._0_5Y_W(in_7), .Money_2(out_8), ._5Y(coin_action_1__5y),
    ._1Y(coin_action_1__1y), ._0_5(coin_action_1__0_5), .Un_money(button_4_out), ._5Y_signal(button_3_out),
    ._1Y_signal(button_2_out), ._0_5Y_signal(button_1_out));  // open: _5Y_Wn, _1Y_Wn, _0_5Y_Wn, Mistake
  assign bit_extender_1_out = {{16{1'b0}}, out_8};  // Bit_Extender bit_extender_1
  Comparator #(.width(32), .mode("twosComplement")) comparator_1 (
    .a(storehouse_module_1_commodity_num), .b({32{1'b0}}), .gt(comparator_1_gt));  // open: eq, lt
  Comparator #(.width(32), .mode("twosComplement")) comparator_2 (
    .a(storehouse_module_1_commodity_price), .b(bit_extender_1_out), .gt(comparator_2_gt));  // open: eq, lt
  not not_1 (not_1_out, comparator_2_gt);
  and and_1 (and_1_out, comparator_1_gt, not_1_out);
  Money_memory money_memory_1 (
    .WE(undriven), .Clk(Clk), ._0_5Y(money_memory_1__0_5y), ._1Y(money_memory_1__1y), ._5Y(money_memory_1__5y));  // open: Addr, Data
  Adder #(.width(32)) adder_1 (.a(money_memory_1__0_5y), .b(bit_extender_2_out), .out(adder_1_out));  // open: cin, cout
  assign bit_extender_2_out = {{16{1'b0}}, coin_action_1__0_5};  // Bit_Extender bit_extender_2
  Adder #(.width(32)) adder_2 (.a(money_memory_1__1y), .b(bit_extender_3_out), .out(adder_2_out));  // open: cin, cout
  assign bit_extender_3_out = {{16{1'b0}}, coin_action_1__1y};  // Bit_Extender bit_extender_3
  Adder #(.width(32)) adder_3 (.a(money_memory_1__5y), .b(bit_extender_4_out), .out(adder_3_out));  // open: cin, cout
  assign bit_extender_4_out = {{16{1'b0}}, coin_action_1__5y};  // Bit_Extender bit_extender_4
endmodule

module display_digital_tube_module (
  input  point,
  input  [15:0] in_2,
  input  unit,
  output point_2,
  output [3:0] Hundreds,
  output [3:0] Tens,
  output [3:0] Ones,
  output [3:0] Decimal,
  output [6:0] out_9,
  output [6:0] out_10,
  output [6:0] out_11
);

  wire [15:0] divider_1_out, divider_1_rem, divider_2_rem, divider_3_rem;
  wire [15:4] divider_2_out, divider_3_out, divider_4_out;

  Divider #(.width(16)) divider_1 (.a(in_2), .b(16'h2), .out(divider_1_out), .rem(divider_1_rem));  // open: upper
  Multiplexer #(.select(1), .width(7), .disabled("Z"), .enable("false")) multiplexer_1 (
    .in0(7'b1010100), .in1(7'b0001000), .out(out_9), .sel(unit));
  Multiplexer #(.select(1), .width(7), .disabled("Z"), .enable("false")) multiplexer_2 (
    .in0(7'b0110100), .in1(7'b0010000), .out(out_10), .sel(unit));
  Divider #(.width(16)) divider_2 (
    .a(divider_1_out), .b(16'h64), .out({divider_2_out, Hundreds}), .rem(divider_2_rem));  // open: upper
  Multiplier #(.width(4)) multiplier_1 (.a(divider_1_rem[3:0]), .b(4'b0101), .out(Decimal));  // open: cin, cout
  Multiplexer #(.select(1), .width(7), .disabled("Z"), .enable("false")) multiplexer_3 (
    .in0(7'b0011111), .in1({7{1'b1}}), .out(out_11), .sel(unit));
  Hex_Digit_Display hex_digit_display_1 (.value(Hundreds));  // open: dp
  Hex_Digit_Display hex_digit_display_2 (.value(Tens));  // open: dp
  Divider #(.width(16)) divider_3 (
    .a(divider_2_rem), .b(16'ha), .out({divider_3_out, Tens}), .rem(divider_3_rem));  // open: upper
  Divider #(.width(16)) divider_4 (.a(divider_3_rem), .b(16'h1), .out({divider_4_out, Ones}));  // open: upper, rem
  Hex_Digit_Display hex_digit_display_3 (.value(Ones), .dp(point));
  Hex_Digit_Display hex_digit_display_4 (.value(Decimal));  // open: dp
  DotMatrix #(.inputtype("column"), .matrixcols(5), .matrixrows(7), .persist(0), .dotshape("square")) dotmatrix_1 (
    .col0(out_9), .col1(out_10), .col2(out_11), .col3(out_10), .col4(out_9));

  assign point_2 = point;

  // Notes on the sheet:
  //   ALL_money*2
endmodule

module Money_memory (
  input  [15:0] Addr,
  input  [31:0] Data,
  input  WE,
  input  Clk,
  output [31:0] _0_5Y,
  output [31:0] _1Y,
  output [31:0] _5Y
);

  wire and_1_out, and_2_out, and_3_out, comparator_1_eq, comparator_2_eq, comparator_3_eq, comparator_4_eq,
       decoder_1_out0, decoder_1_out1, decoder_1_out2, decoder_1_out3, not_1_out, not_2_out, not_3_out,
       not_4_out;
  wire [1:0] counter_1_q;
  wire [15:0] bit_extender_1_out, multiplexer_1_out;
  wire [31:0] demultiplexer_1_out0, demultiplexer_1_out1, demultiplexer_1_out2, demultiplexer_1_out3,
       \存储货币数量_data ;

  Multiplexer #(.select(1), .width(16), .disabled("Z"), .enable("false")) multiplexer_1 (
    .in0(bit_extender_1_out), .in1(Addr), .out(multiplexer_1_out), .sel(WE));
  Counter #(.width(2), .max('h3), .ongoal("wrap"), .trigger("rising"), .behavior("new")) counter_1 (
    .Q(counter_1_q), .clk(Clk), .clr(comparator_1_eq));  // open: load, D, count, carry, preset, down
  assign bit_extender_1_out = {{14{1'b0}}, counter_1_q};  // Bit_Extender bit_extender_1
  Comparator #(.width(2), .mode("twosComplement")) comparator_1 (
    .a(counter_1_q), .b(2'b11), .eq(comparator_1_eq));  // open: gt, lt
  not not_1 (not_1_out, 1'b1);
  RAM #(.addrWidth(16), .dataWidth(32), .bus("separate"), .Select("low")) \u_存储货币数量  (
    .addr(multiplexer_1_out), .din(Data), .data(\存储货币数量_data ), .str(WE), .sel(not_1_out), .clk(Clk),
    .ld(1'b1), .clr(not_1_out));
  Demultiplexer #(.select(2), .width(32), .tristate("false"), .disabled("Z"), .enable("false")) demultiplexer_1 (
    .out0(demultiplexer_1_out0), .out1(demultiplexer_1_out1), .out2(demultiplexer_1_out2),
    .out3(demultiplexer_1_out3), .in(\存储货币数量_data ), .sel(counter_1_q));
  Decoder #(.select(2), .tristate("false"), .disabled(0), .enable("false")) decoder_1 (
    .out0(decoder_1_out0), .out1(decoder_1_out1), .out2(decoder_1_out2), .out3(decoder_1_out3),
    .sel(counter_1_q));
  Comparator #(.width(32), .mode("twosComplement")) comparator_2 (
    .a(demultiplexer_1_out0), .b({32{1'b0}}), .eq(comparator_2_eq));  // open: gt, lt
  Comparator #(.width(32), .mode("twosComplement")) comparator_3 (
    .a({32{1'b0}}), .b(demultiplexer_1_out1), .eq(comparator_3_eq));  // open: gt, lt
  Comparator #(.width(32), .mode("twosComplement")) comparator_4 (
    .a({32{1'b0}}), .b(demultiplexer_1_out2), .eq(comparator_4_eq));  // open: gt, lt
  not not_2 (not_2_out, comparator_2_eq);
  and and_1 (and_1_out, comparator_2_eq, decoder_1_out0);
  not not_3 (not_3_out, comparator_3_eq);
  and and_2 (and_2_out, comparator_3_eq, decoder_1_out1);
  not not_4 (not_4_out, comparator_4_eq);
  and and_3 (and_3_out, comparator_4_eq, decoder_1_out2);
  Register #(.width(32), .trigger("rising"), .Select("low")) u__0_5Y (
    .D(demultiplexer_1_out0), .en(not_2_out), .Q(_0_5Y), .clk(not_2_out), .clr(and_1_out));
  Register #(.width(32), .trigger("rising"), .Select("low")) u__1Y (
    .D(demultiplexer_1_out1), .en(not_3_out), .Q(_1Y), .clk(not_3_out), .clr(and_2_out));
  Register #(.width(32), .trigger("rising"), .Select("low")) u__5Y (
    .D(demultiplexer_1_out2), .en(not_4_out), .Q(_5Y), .clk(not_4_out), .clr(and_3_out));
  Register #(.width(32), .trigger("rising"), .Select("low")) None (
    .D(demultiplexer_1_out3), .clk(decoder_1_out3));  // open: en, Q, clr
endmodule

module storehouse_module (
  input  [15:0] Num,
  input  Wn_signal,
  input  [31:0] Wn_data,
  input  Wp_signal,
  input  [31:0] Wn_data_2,
  input  Clk,
  output [31:0] Commodity_num,
  output [31:0] Commodity_price
);

  wire not_1_out, not_2_out;

  not not_1 (not_1_out, 1'b1);
  not not_2 (not_2_out, 1'b1);
  RAM #(.addrWidth(16), .dataWidth(32), .bus("separate"), .Select("low")) \u_存储数量  (
    .addr(Num), .din(Wn_data), .data(Commodity_num), .str(Wn_signal), .sel(not_1_out), .clk(Clk), .ld(1'b1),
    .clr(not_1_out));
  RAM #(.addrWidth(16), .dataWidth(32), .bus("separate"), .Select("low")) \u_存储价格  (
    .addr(Num), .din(Wn_data_2), .data(Commodity_price), .str(Wp_signal), .sel(not_2_out), .clk(Clk),
    .ld(1'b1), .clr(not_2_out));
endmodule

module Buying_logic (
  input  Clr,
  input  commit,
  input  enable,
  input  [31:0] price,
  input  [31:0] _0_5Y,
  input  [31:0] _1Y,
  input  [31:0] _5Y
);

  wire comparator_1_gt;
  wire [31:0] adder_1_out, adder_2_out, multiplier_1_out, multiplier_2_out;

  Multiplier #(.width(32)) multiplier_1 (.a(_1Y), .b(32'h2), .out(multiplier_1_out));  // open: cin, cout
  Multiplier #(.width(32)) multiplier_2 (.a(_5Y), .b(32'ha), .out(multiplier_2_out));  // open: cin, cout
  Adder #(.width(32)) adder_1 (.a(_0_5Y), .b(multiplier_1_out), .out(adder_1_out));  // open: cin, cout
  Adder #(.width(32)) adder_2 (.a(adder_1_out), .b(multiplier_2_out), .out(adder_2_out));  // open: cin, cout
  Comparator #(.width(32), .mode("twosComplement")) comparator_1 (
    .a(price), .b(adder_2_out), .gt(comparator_1_gt));  // open: eq, lt
endmodule

module test (
  output [31:0] out_1,
  output [31:0] out_2
);

  wire and_1_out, clock_1_out, comparator_1_eq, comparator_2_eq, decoder_1_out0, decoder_1_out1,
       decoder_1_out2, not_1_out, not_2_out, undriven;
  wire [1:0] counter_1_q;
  wire [15:0] bit_extender_1_out;
  wire [31:0] demultiplexer_1_out0, demultiplexer_1_out2, demultiplexer_1_out3, \存储货币数量_data ;

  Clock #(.highDuration(1), .lowDuration(1)) clock_1 (.out(clock_1_out));
  Money_memory money_memory_1 ();  // open: Addr, Data, WE, Clk, _0_5Y, _1Y, _5Y
  Counter #(.width(2), .max('h3), .ongoal("wrap"), .trigger("rising"), .behavior("new")) counter_1 (
    .Q(counter_1_q), .clk(clock_1_out), .clr(comparator_1_eq));  // open: load, D, count, carry, preset, down
  assign bit_extender_1_out = {{14{1'b0}}, counter_1_q};  // Bit_Extender bit_extender_1
  Comparator #(.width(2), .mode("twosComplement")) comparator_1 (
    .a(counter_1_q), .b(2'b11), .eq(comparator_1_eq));  // open: gt, lt
  not not_1 (not_1_out, 1'b1);
  RAM #(.addrWidth(16), .dataWidth(32), .bus("separate"), .Select("low")) \u_存储货币数量  (
    .addr(bit_extender_1_out), .data(\存储货币数量_data ), .str(undriven), .sel(not_1_out), .ld(1'b1),
    .clr(not_1_out));  // open: din, clk
  Demultiplexer #(.select(2), .width(32), .tristate("false"), .disabled("Z"), .enable("false")) demultiplexer_1 (
    .out0(demultiplexer_1_out0), .out2(demultiplexer_1_out2), .out3(demultiplexer_1_out3),
    .in(\存储货币数量_data ), .sel(counter_1_q));  // open: out1
  Decoder #(.select(2), .tristate("false"), .disabled(0), .enable("false")) decoder_1 (
    .out0(decoder_1_out0), .out1(decoder_1_out1), .out2(decoder_1_out2), .sel(counter_1_q));  // open: out3
  Comparator #(.width(32), .mode("twosComplement")) comparator_2 (
    .a(demultiplexer_1_out0), .b({32{1'b0}}), .eq(comparator_2_eq));  // open: gt, lt
  not not_2 (not_2_out, comparator_2_eq);
  and and_1 (and_1_out, comparator_2_eq, decoder_1_out0);
  Register #(.width(32), .trigger("rising"), .Select("low")) _0_5Y (
    .D(demultiplexer_1_out0), .en(not_2_out), .Q(out_1), .clk(not_2_out), .clr(and_1_out));
endmodule
